// Logisim project alu.circ as structural Verilog: 13 circuits, main circuit main
module main (
  input  [3:0] ALUSel,
  input  [31:0] A,
  input  [31:0] B,
  output OverFlow,
  output [31:0] Result,
  output Zero
);

  wire adder_1_out_4, nor_1_out;
  wire [31:0] adder_1_out_3, and_1_out, leftshift_1_out_3, multipliersigned_1_out_3,
       multipliersigned_1_out_4, or_1_out, rshiftsigned_1_out_3, rshiftunsigned_1_out_3, smallerthan_1_out_3,
       smallerthanunsigned_1_out_3, subtractor_1_out_3, unsigned_multiplier_1_p3, xor_1_out;

  adder adder_1 (.in_1(A), .in_2(B), .out_4(adder_1_out_4), .out_3(adder_1_out_3));
  leftshift leftshift_1 (.in_1(A), .in_2(B), .out_3(leftshift_1_out_3));
  smallerthan smallerthan_1 (.in_1(A), .in_2(B), .out_3(smallerthan_1_out_3));
  smallerthanunsigned smallerthanunsigned_1 (.in_1(A), .in_2(B), .out_3(smallerthanunsigned_1_out_3));
  assign xor_1_out = A ^ B;  // XOR_Gate xor_1, 32 bits wide
  rshiftunsigned rshiftunsigned_1 (.in_1(A), .in_2(B), .out_3(rshiftunsigned_1_out_3));
  assign or_1_out = A | B;  // OR_Gate or_1, 32 bits wide
  assign and_1_out = A & B;  // AND_Gate and_1, 32 bits wide
  rshiftsigned rshiftsigned_1 (.in_1(A), .in_2(B), .out_3(rshiftsigned_1_out_3));
  subtractor subtractor_1 (.in_1(A), .in_2(B), .out_3(subtractor_1_out_3));
  multipliersigned multipliersigned_1 (
    .in_1(A), .in_2(B), .out_4(multipliersigned_1_out_4), .out_3(multipliersigned_1_out_3));
  // umult_unsigned_multiplier unsigned_multiplier_1: pin names not known; wires that end beside it: A, B, unsigned_multiplier_1_p3
  mux mux_1 (
    .in_5(adder_1_out_3), .in_6(leftshift_1_out_3), .in_7(smallerthan_1_out_3),
    .in_8(smallerthanunsigned_1_out_3), .in_9(xor_1_out), .in_10(rshiftunsigned_1_out_3), .in_11(or_1_out),
    .in_12(and_1_out), .in_13(multipliersigned_1_out_3), .in_14(multipliersigned_1_out_4),
    .in_16(unsigned_multiplier_1_p3), .in_17(subtractor_1_out_3), .in_18(rshiftsigned_1_out_3), .in_20(B),
    .in_1(ALUSel[3]), .in_2(ALUSel[2]), .in_3(ALUSel[1]), .in_4(ALUSel[0]), .out_21(Result));  // open: in_15, in_19
  nor nor_1 (nor_1_out, ALUSel[0], ALUSel[1], ALUSel[2], ALUSel[3]);
  Comparator #(.width(32)) comparator_1 (.a(Result), .b({32{1'b0}}), .eq(Zero));  // open: gt, lt
  and and_2 (OverFlow, nor_1_out, adder_1_out_4);
endmodule

module converter (
  input  in_1,
  output [31:0] out_2
);

  Multiplier #(.width(32)) multiplier_1 (.a({32{1'b1}}), .b({{31{1'b0}}, in_1}), .out(out_2));  // open: cin, cout
endmodule

module mux (
  input  in_1,
  input  in_2,
  input  in_3,
  input  in_4,
  input  [31:0] in_5,
  input  [31:0] in_6,
  input  [31:0] in_7,
  input  [31:0] in_8,
  input  [31:0] in_9,
  input  [31:0] in_10,
  input  [31:0] in_11,
  input  [31:0] in_12,
  input  [31:0] in_13,
  input  [31:0] in_14,
  input  [31:0] in_15,
  input  [31:0] in_16,
  input  [31:0] in_17,
  input  [31:0] in_18,
  input  [31:0] in_19,
  input  [31:0] in_20,
  output [31:0] out_21
);

  wire not_1_out, not_2_out, not_3_out, not_4_out;
  wire [31:0] and_1_out, and_2_out, and_3_out, and_4_out, and_5_out, and_6_out, and_7_out, and_8_out,
       and_9_out, and_10_out, and_11_out, and_12_out, and_13_out, and_14_out, and_15_out, and_16_out,
       converter_1_out_2, converter_2_out_2, converter_3_out_2, converter_4_out_2, converter_5_out_2,
       converter_6_out_2, converter_7_out_2, converter_8_out_2;

  converter converter_1 (.in_1(in_1), .out_2(converter_1_out_2));
  not not_1 (not_1_out, in_1);
  converter converter_2 (.in_1(not_1_out), .out_2(converter_2_out_2));
  converter converter_3 (.in_1(in_2), .out_2(converter_3_out_2));
  not not_2 (not_2_out, in_2);
  converter converter_4 (.in_1(not_2_out), .out_2(converter_4_out_2));
  converter converter_5 (.in_1(in_3), .out_2(converter_5_out_2));
  not not_3 (not_3_out, in_3);
  converter converter_6 (.in_1(in_4), .out_2(converter_6_out_2));
  converter converter_7 (.in_1(not_3_out), .out_2(converter_7_out_2));
  not not_4 (not_4_out, in_4);
  converter converter_8 (.in_1(not_4_out), .out_2(converter_8_out_2));
  assign and_1_out = converter_8_out_2 & converter_7_out_2 & in_5 & converter_4_out_2 & converter_2_out_2;  // AND_Gate and_1, 32 bits wide
  assign and_2_out = converter_6_out_2 & converter_7_out_2 & in_6 & converter_4_out_2 & converter_2_out_2;  // AND_Gate and_2, 32 bits wide
  assign and_3_out = converter_8_out_2 & converter_5_out_2 & in_7 & converter_4_out_2 & converter_2_out_2;  // AND_Gate and_3, 32 bits wide
  assign and_4_out = converter_6_out_2 & converter_5_out_2 & in_8 & converter_4_out_2 & converter_2_out_2;  // AND_Gate and_4, 32 bits wide
  assign and_5_out = converter_8_out_2 & converter_7_out_2 & in_9 & converter_3_out_2 & converter_2_out_2;  // AND_Gate and_5, 32 bits wide
  assign and_6_out = converter_6_out_2 & converter_7_out_2 & in_10 & converter_3_out_2 & converter_2_out_2;  // AND_Gate and_6, 32 bits wide
  assign and_7_out = converter_8_out_2 & converter_5_out_2 & in_11 & converter_3_out_2 & converter_2_out_2;  // AND_Gate and_7, 32 bits wide
  assign and_8_out = converter_6_out_2 & converter_5_out_2 & in_12 & converter_3_out_2 & converter_2_out_2;  // AND_Gate and_8, 32 bits wide
  assign and_9_out = converter_8_out_2 & converter_7_out_2 & in_13 & converter_4_out_2 & converter_1_out_2;  // AND_Gate and_9, 32 bits wide
  assign and_10_out = converter_6_out_2 & converter_7_out_2 & in_14 & converter_4_out_2 & converter_1_out_2;  // AND_Gate and_10, 32 bits wide
  assign and_11_out = converter_8_out_2 & converter_5_out_2 & in_15 & converter_4_out_2 & converter_1_out_2;  // AND_Gate and_11, 32 bits wide
  assign and_12_out = converter_6_out_2 & converter_5_out_2 & in_16 & converter_4_out_2 & converter_1_out_2;  // AND_Gate and_12, 32 bits wide
  assign and_13_out = converter_8_out_2 & converter_7_out_2 & in_17 & converter_3_out_2 & converter_1_out_2;  // AND_Gate and_13, 32 bits wide
  assign and_14_out = converter_6_out_2 & converter_7_out_2 & in_18 & converter_3_out_2 & converter_1_out_2;  // AND_Gate and_14, 32 bits wide
  assign and_15_out = converter_8_out_2 & converter_5_out_2 & in_19 & converter_3_out_2 & converter_1_out_2;  // AND_Gate and_15, 32 bits wide
  assign and_16_out = converter_6_out_2 & converter_5_out_2 & in_20 & converter_3_out_2 & converter_1_out_2;  // AND_Gate and_16, 32 bits wide
  assign out_21 = and_1_out | and_2_out | and_3_out | and_4_out | and_5_out | and_6_out | and_7_out | and_8_out | and_9_out | and_10_out | and_11_out | and_12_out | and_13_out | and_14_out | and_15_out | and_16_out;  // OR_Gate or_1, 32 bits wide
endmodule

module adder (
  input  [31:0] in_1,
  input  [31:0] in_2,
  output [31:0] out_3,
  output out_4
);

  wire adder_1_cout, and_2_out, xnor_1_out, xor_1_out;

  Adder #(.width(32)) adder_1 (.a(in_1), .b(in_2), .out(out_3), .cin(1'b0), .cout(adder_1_cout));
  and and_1 (out_4, adder_1_cout, and_2_out);
  xnor xnor_1 (xnor_1_out, in_1[31], in_2[31]);
  xor xor_1 (xor_1_out, in_2[31], out_3[31]);
  and and_2 (and_2_out, xnor_1_out, xor_1_out);
endmodule

module subtractor (
  input  [31:0] in_1,
  input  [31:0] in_2,
  output [31:0] out_3
);

  Subtractor #(.width(32)) subtractor_1 (.a(in_1), .b(in_2), .out(out_3), .bin(1'b0));  // open: bout
endmodule

module leftshift (
  input  [31:0] in_1,
  input  [31:0] in_2,
  output [31:0] out_3
);

  Shifter #(.width(32)) shifter_1 (.in(in_1), .\dist (in_2[4:0]), .out(out_3));
endmodule

module rshiftunsigned (
  input  [31:0] in_1,
  input  [31:0] in_2,
  output [31:0] out_3
);

  Shifter #(.width(32), .shift("lr")) shifter_1 (.in(in_1), .\dist (in_2[4:0]), .out(out_3));
endmodule

module rshiftsigned (
  input  [31:0] in_1,
  input  [31:0] in_2,
  output [31:0] out_3
);

  Shifter #(.width(32), .shift("ar")) shifter_1 (.in(in_1), .\dist (in_2[4:0]), .out(out_3));
endmodule

module signedmul (
  input  [31:0] in_1,
  input  [31:0] in_2,
  output [31:0] out_3,
  output [31:0] out_4
);

  Multiplier #(.width(32)) multiplier_1 (.a(in_1), .b(in_2), .out(out_3), .cin({32{1'b0}}), .cout(out_4));
endmodule

module smallerthan (
  input  [31:0] in_1,
  input  [31:0] in_2,
  output [31:0] out_3
);

  wire comparator_1_lt;

  Comparator #(.width(32)) comparator_1 (.a(in_1), .b(in_2), .lt(comparator_1_lt));  // open: gt, eq
  assign out_3 = {{31{1'b0}}, comparator_1_lt};  // Bit_Extender bit_extender_1
endmodule

module multipliersigned (
  input  [31:0] in_1,
  input  [31:0] in_2,
  output [31:0] out_3,
  output [31:0] out_4
);

  Multiplier #(.width(32)) multiplier_1 (.a(in_1), .b(in_2), .out(out_3), .cin({32{1'b0}}), .cout(out_4));
endmodule

module unsigned_multiplier (
  input  [31:0] in_1,
  input  [31:0] in_2,
  output [31:0] out_3
);

  wire adder_2_cout, adder_3_cout, and_1_out, subtractor_1_bout;
  wire [31:0] adder_1_out, adder_2_out, adder_3_out, adder_4_out, adder_5_out, bit_extender_1_out,
       bit_extender_2_out, bit_extender_3_out, bit_extender_4_out, bit_extender_5_out, bit_extender_6_out,
       multiplier_1_cout, multiplier_1_out, multiplier_2_out, multiplier_3_out, shifter_1_out, shifter_2_out,
       shifter_3_out, shifter_4_out, shifter_5_out;

  Shifter #(.width(32), .shift("lr")) shifter_1 (.in(in_1), .\dist (5'b00001), .out(shifter_1_out));
  Shifter #(.width(32), .shift("lr")) shifter_2 (.in(in_2), .\dist (5'b00001), .out(shifter_2_out));
  assign bit_extender_1_out = {{31{1'b0}}, in_1[0]};  // Bit_Extender bit_extender_1
  Multiplier #(.width(32)) multiplier_1 (
    .a(shifter_1_out), .b(shifter_2_out), .out(multiplier_1_out), .cin({32{1'b0}}), .cout(multiplier_1_cout));
  assign bit_extender_2_out = {{31{1'b0}}, in_2[0]};  // Bit_Extender bit_extender_2
  Multiplier #(.width(32)) multiplier_2 (.a(in_1), .b(bit_extender_2_out), .out(multiplier_2_out));  // open: cin, cout
  Multiplier #(.width(32)) multiplier_3 (.a(bit_extender_1_out), .b(in_2), .out(multiplier_3_out));  // open: cin, cout
  Shifter #(.width(32)) shifter_3 (.in(multiplier_1_cout), .\dist (5'b00010), .out(shifter_3_out));
  and and_1 (and_1_out, in_2[0], in_1[0]);
  Shifter #(.width(32)) shifter_4 (.in(multiplier_1_out), .\dist (5'b00010), .out(shifter_4_out));
  Shifter #(.width(32), .shift("lr")) shifter_5 (.in(multiplier_1_out), .\dist (5'b11110), .out(shifter_5_out));
  assign bit_extender_3_out = {{31{1'b0}}, and_1_out};  // Bit_Extender bit_extender_3
  Adder #(.width(32)) adder_1 (.a(shifter_5_out), .b(shifter_3_out), .out(adder_1_out));  // open: cin, cout
  Adder #(.width(32)) adder_2 (
    .a(multiplier_3_out), .b(shifter_4_out), .out(adder_2_out), .cin(1'b0), .cout(adder_2_cout));
  Subtractor #(.width(32)) subtractor_1 (
    .a(adder_3_out), .b(bit_extender_3_out), .bin(1'b0), .bout(subtractor_1_bout));  // open: out
  assign bit_extender_4_out = {{31{1'b0}}, subtractor_1_bout};  // Bit_Extender bit_extender_4
  Adder #(.width(32)) adder_3 (
    .a(multiplier_2_out), .b(adder_2_out), .out(adder_3_out), .cin(1'b0), .cout(adder_3_cout));
  assign bit_extender_5_out = {{31{1'b0}}, adder_2_cout};  // Bit_Extender bit_extender_5
  Adder #(.width(32)) adder_4 (.a(bit_extender_5_out), .b(adder_1_out), .out(adder_4_out), .cin(1'b0));  // open: cout
  Subtractor #(.width(32)) subtractor_2 (.a(adder_5_out), .b(bit_extender_4_out), .out(out_3));  // open: bin, bout
  assign bit_extender_6_out = {{31{1'b0}}, adder_3_cout};  // Bit_Extender bit_extender_6
  Adder #(.width(32)) adder_5 (.a(bit_extender_6_out), .b(adder_4_out), .out(adder_5_out));  // open: cin, cout
endmodule

module smallerthanunsigned (
  input  [31:0] in_1,
  input  [31:0] in_2,
  output [31:0] out_3
);

  wire comparator_1_lt;

  Comparator #(.width(32), .mode("unsigned")) comparator_1 (.a(in_1), .b(in_2), .lt(comparator_1_lt));  // open: gt, eq
  assign out_3 = {{31{1'b0}}, comparator_1_lt};  // Bit_Extender bit_extender_1
endmodule
