// Logisim project processor.circ as structural Verilog: 8 circuits, main circuit decode
module decode (
  input  [31:0] in_1,
  output PC_src_bb172d66,
  output [4:0] Wr_idx_294427e2,
  output [4:0] R1_idx_2ee4a04b,
  output [4:0] R2_idx_f2d9e592,
  output [31:0] Imm,
  output write,
  output [3:0] ALUop,
  output ALUsrc,
  output write_src_a92b7672,
  output mem_ld_42990892,
  output mem_str_d58406d3
);

  wire nor_2_out;

  or or_1 (write_src_a92b7672, in_1[4], in_1[5]);
  imm imm_1 (.in_1(in_1), .out_2(Imm));
  nor nor_1 (mem_ld_42990892, in_1[5], in_1[4]);
  nor nor_2 (nor_2_out, in_1[5], in_1[6], in_1[4]);
  aluop aluop_1 (.in_1(in_1), .out_2(ALUop));
  and and_1 (mem_str_d58406d3, ~in_1[6], in_1[5], ~in_1[4]);  // AND_Gate
  or or_2 (write, nor_2_out, in_1[4]);
  Multiplexer #(.select(3), .enable("false")) multiplexer_1 (
    .in0(1'b0), .in1(1'b0), .in2(1'b0), .in3(1'b1), .in4(1'b0), .in5(1'b0), .in6(1'b1), .in7(1'b0),
    .out(ALUsrc), .sel(in_1[6:4]));

  assign PC_src_bb172d66 = in_1[6];
  assign R1_idx_2ee4a04b = in_1[19:15];
  assign R2_idx_f2d9e592 = in_1[24:20];
  assign Wr_idx_294427e2 = in_1[11:7];
endmodule

module imm (
  input  [31:0] in_1,
  output [31:0] out_2
);

  wire [31:0] bit_extender_1_out, bit_extender_2_out, bit_extender_3_out;

  assign bit_extender_1_out = {{20{1'b0}}, in_1[31:20]};  // Bit_Extender bit_extender_1
  assign bit_extender_2_out = {{19{1'b0}}, {in_1[31], in_1[7], in_1[30:25], in_1[11:8], 1'b0}};  // Bit_Extender bit_extender_2
  assign bit_extender_3_out = {{20{1'b0}}, {in_1[31:25], in_1[11:7]}};  // Bit_Extender bit_extender_3
  Multiplexer #(.select(2), .width(32), .enable("false")) multiplexer_1 (
    .in0(bit_extender_1_out), .in1(bit_extender_3_out), .in2({32{1'b0}}), .in3(bit_extender_2_out),
    .out(out_2), .sel(in_1[6:5]));
endmodule

module aluop (
  input  [31:0] in_1,
  output [3:0] out_2
);

  wire and_1_out, not_1_out, not_2_out, not_3_out;
  wire [3:0] bit_extender_1_out, bit_extender_2_out, multiplexer_1_out, multiplexer_2_out;

  assign bit_extender_1_out = {{1{1'b0}}, in_1[14:12]};  // Bit_Extender bit_extender_1
  assign bit_extender_2_out = {{1{1'b0}}, in_1[14:12]};  // Bit_Extender bit_extender_2
  not not_1 (not_1_out, in_1[12]);
  not not_2 (not_2_out, in_1[13]);
  not not_3 (not_3_out, in_1[14]);
  and and_1 (and_1_out, not_1_out, not_2_out, not_3_out);
  Multiplexer #(.width(4), .enable("false")) multiplexer_1 (
    .in0(4'b0000), .in1(4'b1100), .out(multiplexer_1_out), .sel(in_1[30]));
  Multiplexer #(.width(4), .enable("false")) multiplexer_2 (
    .in0(bit_extender_2_out), .in1(multiplexer_1_out), .out(multiplexer_2_out), .sel(and_1_out));
  Multiplexer #(.select(3), .width(4), .enable("false")) multiplexer_3 (
    .in0(4'b0000), .in1(bit_extender_1_out), .in2(4'b0000), .in3(multiplexer_2_out), .in6(4'b1100),
    .out(out_2), .sel(in_1[6:4]));  // open: in4, in5, in7
endmodule

module processor (
  input  clk,
  input  clear,
  output [4:0] rd,
  output [4:0] rs1,
  output [31:0] Op2,
  output [31:0] Res,
  output [31:0] memout,
  output write,
  output [3:0] op,
  output [4:0] rs2,
  output [31:0] op1,
  output [31:0] Imm,
  output [31:0] Instr
);

  wire and_1_out, decode_1_alusrc, decode_1_mem_ld_42990892, decode_1_mem_str_d58406d3,
       decode_1_pc_src_bb172d66, decode_1_write_src_a92b7672, main_1_zero;
  wire [23:0] adder_1_out, adder_2_out, multiplexer_1_out, register_1_q;
  wire [31:0] multiplexer_3_out, register_2_read_data_2;

  Register #(.width(24)) register_1 (.D(multiplexer_1_out), .en(1'b1), .Q(register_1_q), .clk(clk), .clr(clear));
  ROM #(.addrWidth(24), .dataWidth(32)) rom_1 (.addr(register_1_q), .data(Instr), .sel(1'b1));
  Adder #(.width(24)) adder_1 (.a(register_1_q), .b(24'h4), .out(adder_1_out));  // open: cin, cout
  Adder #(.width(24)) adder_2 (.a(register_1_q), .b(Imm[23:0]), .out(adder_2_out));  // open: cin, cout
  decode decode_1 (
    .in_1(Instr), .PC_src_bb172d66(decode_1_pc_src_bb172d66),
    .write_src_a92b7672(decode_1_write_src_a92b7672), .mem_ld_42990892(decode_1_mem_ld_42990892),
    .mem_str_d58406d3(decode_1_mem_str_d58406d3), .Wr_idx_294427e2(rd), .R1_idx_2ee4a04b(rs1),
    .R2_idx_f2d9e592(rs2), .Imm(Imm), .write(write), .ALUop(op), .ALUsrc(decode_1_alusrc));
  Multiplexer #(.width(24), .enable("false")) multiplexer_1 (
    .in0(adder_1_out), .in1(adder_2_out), .out(multiplexer_1_out), .sel(and_1_out));
  and and_1 (and_1_out, decode_1_pc_src_bb172d66, main_1_zero);
  register register_2 (
    .Write_Register(rd), .Write_Data(multiplexer_3_out), .Clock(clk), .RegWEn(write), .Read_Register_1(rs1),
    .Read_Data_1(op1), .Read_Data_2(register_2_read_data_2), .Read_Register_2(rs2));
  Multiplexer #(.width(32), .enable("false")) multiplexer_2 (
    .in0(Imm), .in1(register_2_read_data_2), .out(Op2), .sel(decode_1_alusrc));
  Multiplexer #(.width(32), .enable("false")) multiplexer_3 (
    .in0(memout), .in1(Res), .out(multiplexer_3_out), .sel(decode_1_write_src_a92b7672));
  alu_main main_1 (.A(op1), .B(Op2), .ALUSel(op), .Result(Res), .Zero(main_1_zero));  // open: OverFlow
  RAM #(.addrWidth(24), .dataWidth(32), .bus("separate")) ram_1 (
    .addr(Res[23:0]), .din(register_2_read_data_2), .data(memout), .str(decode_1_mem_str_d58406d3),
    .sel(1'b1), .clk(clk), .ld(decode_1_mem_ld_42990892), .clr(clear));

  // Notes on the sheet:
  //   contents of rom_1 (hex, n*v repeats v):
  //   4*0 c800313 0 0 0 62b3b3 0 0 0 6428293 0 0 0 628463 0 0 0 f9c28293 0 0 0 6428293 0 0 0 c830313 0 0 0
  //   5020a3 0 0 0 602123
endmodule

module _2x4_dec (
  input  in_1,
  input  in_2,
  input  in_3,
  output out_4,
  output out_5,
  output out_6,
  output out_7
);

  wire not_1_out, not_2_out;

  not not_1 (not_1_out, in_1);
  not not_2 (not_2_out, in_2);
  and and_1 (out_4, not_1_out, in_3, not_2_out);
  and and_2 (out_5, not_1_out, in_3, in_2);
  and and_3 (out_6, not_2_out, in_3, in_1);
  and and_4 (out_7, in_1, in_3, in_2);
endmodule

module _3x8_dec (
  input  in_1,
  input  in_2,
  input  in_3,
  input  in_4,
  output out_5,
  output out_6,
  output out_7,
  output out_8,
  output out_9,
  output out_10,
  output out_11,
  output out_12
);

  wire and_1_out, and_2_out, not_1_out;

  not not_1 (not_1_out, in_1);
  and and_1 (and_1_out, not_1_out, in_4);
  and and_2 (and_2_out, in_1, in_4);
  _2x4_dec u_2x4_dec_1 (
    .in_1(in_2), .in_2(in_3), .in_3(and_1_out), .out_4(out_5), .out_5(out_6), .out_6(out_7), .out_7(out_8));
  _2x4_dec u_2x4_dec_2 (
    .in_1(in_2), .in_2(in_3), .in_3(and_2_out), .out_4(out_9), .out_5(out_10), .out_6(out_11), .out_7(out_12));
endmodule

module _5x32_dec (
  input  in_1,
  input  in_2,
  input  in_3,
  input  in_4,
  input  in_5,
  input  in_6,
  output out_7,
  output out_8,
  output out_9,
  output out_10,
  output out_11,
  output out_12,
  output out_13,
  output out_14,
  output out_15,
  output out_16,
  output out_17,
  output out_18,
  output out_19,
  output out_20,
  output out_21,
  output out_22,
  output out_23,
  output out_24,
  output out_25,
  output out_26,
  output out_27,
  output out_28,
  output out_29,
  output out_30,
  output out_31,
  output out_32,
  output out_33,
  output out_34,
  output out_35,
  output out_36,
  output out_37,
  output out_38
);

  wire n2x4_dec_1_out_4, n2x4_dec_1_out_5, n2x4_dec_1_out_6, n2x4_dec_1_out_7;

  _2x4_dec u_2x4_dec_1 (
    .in_1(in_1), .in_2(in_2), .in_3(in_6), .out_4(n2x4_dec_1_out_4), .out_5(n2x4_dec_1_out_5),
    .out_6(n2x4_dec_1_out_6), .out_7(n2x4_dec_1_out_7));
  _3x8_dec u_3x8_dec_1 (
    .in_1(in_3), .in_2(in_4), .in_3(in_5), .in_4(n2x4_dec_1_out_4), .out_5(out_7), .out_6(out_8),
    .out_7(out_9), .out_8(out_10), .out_9(out_11), .out_10(out_12), .out_11(out_13), .out_12(out_14));
  _3x8_dec u_3x8_dec_2 (
    .in_1(in_3), .in_2(in_4), .in_3(in_5), .in_4(n2x4_dec_1_out_6), .out_5(out_22), .out_6(out_24),
    .out_7(out_25), .out_8(out_26), .out_9(out_27), .out_10(out_28), .out_11(out_29), .out_12(out_30));
  _3x8_dec u_3x8_dec_3 (
    .in_1(in_3), .in_2(in_4), .in_3(in_5), .in_4(n2x4_dec_1_out_5), .out_5(out_15), .out_6(out_16),
    .out_7(out_17), .out_8(out_18), .out_9(out_19), .out_10(out_20), .out_11(out_21), .out_12(out_23));
  _3x8_dec u_3x8_dec_4 (
    .in_1(in_3), .in_2(in_4), .in_3(in_5), .in_4(n2x4_dec_1_out_7), .out_5(out_31), .out_6(out_32),
    .out_7(out_33), .out_8(out_34), .out_9(out_35), .out_10(out_36), .out_11(out_37), .out_12(out_38));
endmodule

module register (
  input  Clock,
  input  [4:0] Read_Register_1,
  input  [31:0] Write_Data,
  input  [4:0] Write_Register,
  input  RegWEn,
  input  [4:0] Read_Register_2,
  output [31:0] Read_Data_1,
  output [31:0] Read_Data_2
);

  wire n5x32_dec_1_out_8, n5x32_dec_1_out_9, n5x32_dec_1_out_12, n5x32_dec_1_out_13, n5x32_dec_1_out_14,
       n5x32_dec_1_out_15, n5x32_dec_1_out_16, n5x32_dec_1_out_17;
  wire [31:0] ra_q, register_1_q, s0_q, s1_q, sp_q, t0_q, t1_q, t2_q;

  _5x32_dec u_5x32_dec_1 (
    .in_1(Write_Register[4]), .in_2(Write_Register[3]), .in_3(Write_Register[2]), .in_4(Write_Register[1]),
    .in_5(Write_Register[0]), .in_6(RegWEn), .out_8(n5x32_dec_1_out_8), .out_9(n5x32_dec_1_out_9),
    .out_12(n5x32_dec_1_out_12), .out_13(n5x32_dec_1_out_13), .out_14(n5x32_dec_1_out_14),
    .out_15(n5x32_dec_1_out_15), .out_16(n5x32_dec_1_out_16), .out_17(n5x32_dec_1_out_17));  // open: out_7, out_10, out_11, out_18, out_19, out_20, out_21, out_22, out_23, out_24, out_25, out_26, out_27, out_28, out_29, out_30, out_31, out_32, out_33, out_34, out_35, out_36, out_37, out_38
  Register #(.width(32)) ra (.D(Write_Data), .en(n5x32_dec_1_out_8), .Q(ra_q), .clk(Clock));  // open: clr
  Register #(.width(32)) sp (.D(Write_Data), .en(n5x32_dec_1_out_9), .Q(sp_q), .clk(Clock));  // open: clr
  Register #(.width(32)) t0 (.D(Write_Data), .en(n5x32_dec_1_out_12), .Q(t0_q), .clk(Clock));  // open: clr
  Register #(.width(32)) t1 (.D(Write_Data), .en(n5x32_dec_1_out_13), .Q(t1_q), .clk(Clock));  // open: clr
  Register #(.width(32)) t2 (.D(Write_Data), .en(n5x32_dec_1_out_14), .Q(t2_q), .clk(Clock));  // open: clr
  Register #(.width(32)) s0 (.D(Write_Data), .en(n5x32_dec_1_out_15), .Q(s0_q), .clk(Clock));  // open: clr
  Register #(.width(32)) s1 (.D(Write_Data), .en(n5x32_dec_1_out_16), .Q(s1_q), .clk(Clock));  // open: clr
  Register #(.width(32)) register_1 (
    .D(Write_Data), .en(n5x32_dec_1_out_17), .Q(register_1_q), .clk(Clock));  // open: clr
  Multiplexer #(.select(5), .width(32)) multiplexer_1 (
    .in0({32{1'b0}}), .in1(ra_q), .in2(sp_q), .in5(t0_q), .in6(t1_q), .in7(t2_q), .in8(s0_q), .in9(s1_q),
    .in10(register_1_q), .out(Read_Data_1), .sel(Read_Register_1), .en(1'b1));  // open: in3, in4, in11, in12, in13, in14, in15, in16, in17, in18, in19, in20, in21, in22, in23, in24, in25, in26, in27, in28, in29, in30, in31
  Multiplexer #(.select(5), .width(32)) multiplexer_2 (
    .in0({32{1'b0}}), .in1(ra_q), .in2(sp_q), .in5(t0_q), .in6(t1_q), .in7(t2_q), .in8(s0_q), .in9(s1_q),
    .in10(register_1_q), .out(Read_Data_2), .sel(Read_Register_2), .en(1'b1));  // open: in3, in4, in11, in12, in13, in14, in15, in16, in17, in18, in19, in20, in21, in22, in23, in24, in25, in26, in27, in28, in29, in30, in31
endmodule
